// Logisim project solution-3.circ as structural Verilog: 1 circuit, main circuit main
module main (
  input  in_1,
  output out_2,
  output out_3,
  output out_4,
  output out_5
);

  wire and_1_out, clock_1_out, t_ff_1_qn, t_ff_2_qn, t_ff_3_qn;

  Clock clock_1 (.out(clock_1_out));
  T_Flip_Flop t_ff_1 (.clk(clock_1_out), .T(in_1), .Q(out_5), .Qn(t_ff_1_qn), .reset(and_1_out));  // open: preset, en
  T_Flip_Flop t_ff_2 (.clk(t_ff_1_qn), .T(in_1), .Q(out_4), .Qn(t_ff_2_qn), .reset(and_1_out));  // open: preset, en
  T_Flip_Flop t_ff_3 (.clk(t_ff_2_qn), .T(in_1), .Q(out_3), .Qn(t_ff_3_qn), .reset(and_1_out));  // open: preset, en
  T_Flip_Flop t_ff_4 (.clk(t_ff_3_qn), .T(in_1), .Q(out_2), .reset(and_1_out));  // open: Qn, preset, en
  Hex_Digit_Display hex_digit_display_1 (.value({out_2, out_3, out_4, out_5}));  // open: dp
  and and_1 (and_1_out, out_2, out_4);
endmodule
